// Logisim project trabalhologico.circ as structural Verilog
module questao1a (
  input  A,
  input  B,
  input  C,
  output X
);

  wire nand_1_out, nand_2_out, nand_3_out;

  nand nand_1 (nand_1_out, 1'b1, A);
  nand nand_2 (nand_2_out, 1'b1, C);
  nand nand_3 (nand_3_out, nand_1_out, B);
  nand nand_4 (X, nand_2_out, nand_3_out);
endmodule

module questao1b (
  input  A,
  input  B,
  input  C,
  output X
);

  wire nand_1_out, nand_2_out, nand_3_out;

  nand nand_1 (nand_1_out, 1'b1, B);
  nand nand_2 (nand_2_out, 1'b1, C);
  nand nand_3 (nand_3_out, A, nand_2_out);
  nand nand_4 (X, nand_1_out, nand_3_out);
endmodule

module questao1c (
  input  A,
  input  B,
  input  C,
  input  D,
  output X
);

  wire nand_1_out, nand_2_out, nand_3_out, nand_4_out, nand_5_out, nand_6_out, nand_7_out, nand_8_out;

  nand nand_1 (nand_1_out, 1'b1, A);
  nand nand_2 (nand_2_out, 1'b1, B);
  nand nand_3 (nand_3_out, 1'b1, C);
  nand nand_4 (nand_4_out, 1'b1, D);
  nand nand_5 (nand_5_out, nand_1_out, C);
  nand nand_6 (nand_6_out, nand_1_out, D);
  nand nand_7 (nand_7_out, A, nand_2_out, nand_3_out);
  nand nand_8 (nand_8_out, B, nand_3_out, nand_4_out);
  nand nand_9 (X, nand_5_out, nand_6_out, nand_7_out, nand_8_out);
endmodule

module questao1d (
  input  A,
  input  B,
  input  C,
  output X,
  output Y
);

  wire and_1_out, and_2_out, and_3_out;

  xor odd_parity_1 (X, A, B, C);
  and and_1 (and_1_out, B, C);
  and and_2 (and_2_out, A, C);
  or or_1 (Y, and_1_out, and_2_out, and_3_out);
  and and_3 (and_3_out, A, B);
endmodule

module questao2a (
  input  A,
  input  B,
  input  C,
  output X
);

  and and_1 (X, A, B, C);
endmodule

module questao2b (
  input  A,
  input  B,
  input  C,
  input  D,
  output X
);

  wire and_1_out, and_2_out, and_3_out, and_4_out, not_1_out, not_2_out, not_3_out, not_4_out;

  not not_1 (not_1_out, A);
  not not_2 (not_2_out, B);
  not not_3 (not_3_out, C);
  not not_4 (not_4_out, D);
  and and_1 (and_1_out, not_1_out, not_2_out, not_3_out, D);
  and and_2 (and_2_out, not_1_out, not_2_out, C, not_4_out);
  and and_3 (and_3_out, not_1_out, B, not_3_out, not_4_out);
  and and_4 (and_4_out, A, B, C);
  or or_1 (X, and_1_out, and_2_out, and_3_out, and_4_out);
endmodule

module questao3 (
  input  A,
  input  B,
  input  C,
  input  D,
  output Y
);

  wire and_1_out, and_2_out, and_3_out, not_1_out, not_2_out, not_3_out, not_4_out;

  not not_1 (not_1_out, A);
  not not_2 (not_2_out, B);
  not not_3 (not_3_out, C);
  not not_4 (not_4_out, D);
  and and_1 (and_1_out, not_1_out, not_2_out);
  and and_2 (and_2_out, not_2_out, not_4_out);
  and and_3 (and_3_out, A, B, not_3_out, D);
  or or_1 (Y, and_1_out, and_2_out, and_3_out);
endmodule

module questao4 (
  input  H,
  input  U,
  input  T,
  input  F,
  output A
);

  wire and_1_out, and_2_out;

  and and_1 (and_1_out, T, H);
  and and_2 (and_2_out, F, U);
  or or_1 (A, and_1_out, and_2_out);
endmodule

module questao5 (
  input  B2,
  input  B1,
  input  B0,
  output Y3,
  output Y2,
  output Y1,
  output Y0
);

  wire not_1_out;

  not not_1 (not_1_out, B1);
  and and_1 (Y3, B2, B1);
  and and_2 (Y2, B2, not_1_out);
  xor xor_1 (Y1, B0, B1);

  assign Y0 = 1'b1;
endmodule
